# Fritzing sketch ParticleAlexa (saved by Fritzing 0.9.10b)
breadboards: 1

parts:
  Part1 = Photon
  DHT1 = DHT11 Humitidy and Temperature Sensor
  R1 = Resistor [tolerance=±5% power=0.25 resistance=10k package=THT]
  LED2 = smd LED [color="Red (633nm)" package="0805 [SMD]"]
  LED3 = smd LED [color="Green (565nm)" package="0805 [SMD]"]
  R2 = Resistor [tolerance=±5% power=0.25 resistance=10 package=THT]
  R3 = Resistor [tolerance=±5% power=0.25 resistance=82 package=THT]

nets:
  GND: Part1.GND, DHT1.GND, LED2.cathode, LED3.cathode
  N1: Part1.D2, R3.Pin_0
  N2: Part1.D4, DHT1.DATA, R1.Pin_1
  N3: Part1.D6, R2.Pin_0
  3V3: Part1.3V3, DHT1.VDD, R1.Pin_0
  N4: LED2.anode, R3.Pin_1
  N5: LED3.anode, R2.Pin_1

custom parts:
  DHT11 Humitidy and Temperature Sensor: DHT11 Humidity and Temperature Sensor
